// Logisim project Spagetti_8_Bit.circ as structural Verilog: 7 circuits, main circuit main
module main (
  input  RESET
);

  wire clock_1_out, controlunit_1_ac_to_bus_en, controlunit_1_ac_we, controlunit_1_ir_we,
       controlunit_1_mar_we, controlunit_1_pc_load, controlunit_1_pc_to_bus_en, controlunit_1_pc_we,
       controlunit_1_ram_oe, controlunit_1_ram_we;
  wire [2:0] controlunit_1_alu_sel;
  wire [7:0] AC_q, alu_1_result, controlled_buffer_7_out, IR_q, MAR_q, programcounter_1_pc_out;

  Clock clock_1 (.out(clock_1_out));
  ControlUnit controlunit_1 (
    .OPCODE(IR_q[7:4]), .CLK(clock_1_out), .RESET(RESET), .ALU_SEL(controlunit_1_alu_sel),
    .PC_Load(controlunit_1_pc_load), .PC_WE(controlunit_1_pc_we), .AC_WE(controlunit_1_ac_we),
    .IR_WE(controlunit_1_ir_we), .MAR_WE(controlunit_1_mar_we), .RAM_WE(controlunit_1_ram_we),
    .RAM_OE(controlunit_1_ram_oe), .AC_to_Bus_EN(controlunit_1_ac_to_bus_en),
    .PC_to_Bus_EN(controlunit_1_pc_to_bus_en));  // open: COUNTER_RESET
  Register8bit AC (.WE(controlunit_1_ac_we), .D(alu_1_result), .CLK(clock_1_out), .Q(AC_q));
  Register8bit IR (.WE(controlunit_1_ir_we), .D(controlled_buffer_7_out), .CLK(clock_1_out), .Q(IR_q));
  Register8bit MAR (
    .WE(controlunit_1_mar_we), .D(controlled_buffer_7_out), .CLK(clock_1_out),
    .Q({MAR_q[0], MAR_q[1], MAR_q[2], MAR_q[3], MAR_q[4], MAR_q[5], MAR_q[6], MAR_q[7]}));
  ALU alu_1 (
    .A(AC_q), .B(controlled_buffer_7_out), .ALU_SEL(controlunit_1_alu_sel), .Result(alu_1_result));  // open: CarryOut, Zero
  assign controlled_buffer_7_out[6] = controlunit_1_ac_to_bus_en ? AC_q[6] : 1'bz;  // Controlled_Buffer controlled_buffer_1
  assign controlled_buffer_7_out[7] = controlunit_1_ac_to_bus_en ? AC_q[7] : 1'bz;  // Controlled_Buffer controlled_buffer_2
  assign controlled_buffer_7_out[2] = controlunit_1_ac_to_bus_en ? AC_q[2] : 1'bz;  // Controlled_Buffer controlled_buffer_3
  assign controlled_buffer_7_out[3] = controlunit_1_ac_to_bus_en ? AC_q[3] : 1'bz;  // Controlled_Buffer controlled_buffer_4
  assign controlled_buffer_7_out[4] = controlunit_1_ac_to_bus_en ? AC_q[4] : 1'bz;  // Controlled_Buffer controlled_buffer_5
  assign controlled_buffer_7_out[5] = controlunit_1_ac_to_bus_en ? AC_q[5] : 1'bz;  // Controlled_Buffer controlled_buffer_6
  assign controlled_buffer_7_out[0] = controlunit_1_ac_to_bus_en ? AC_q[0] : 1'bz;  // Controlled_Buffer controlled_buffer_7
  assign controlled_buffer_7_out[1] = controlunit_1_ac_to_bus_en ? AC_q[1] : 1'bz;  // Controlled_Buffer controlled_buffer_8
  assign controlled_buffer_7_out[7] = controlunit_1_pc_to_bus_en ? programcounter_1_pc_out[7] : 1'bz;  // Controlled_Buffer controlled_buffer_9
  ProgramCounter programcounter_1 (
    .PC_Load(controlunit_1_pc_load), .PC_WE(controlunit_1_pc_we), .CLK(clock_1_out),
    .Data_IN(controlled_buffer_7_out), .PC_OUT(programcounter_1_pc_out));
  assign controlled_buffer_7_out[3] = controlunit_1_pc_to_bus_en ? programcounter_1_pc_out[3] : 1'bz;  // Controlled_Buffer controlled_buffer_10
  assign controlled_buffer_7_out[4] = controlunit_1_pc_to_bus_en ? programcounter_1_pc_out[4] : 1'bz;  // Controlled_Buffer controlled_buffer_11
  assign controlled_buffer_7_out[5] = controlunit_1_pc_to_bus_en ? programcounter_1_pc_out[5] : 1'bz;  // Controlled_Buffer controlled_buffer_12
  assign controlled_buffer_7_out[6] = controlunit_1_pc_to_bus_en ? programcounter_1_pc_out[6] : 1'bz;  // Controlled_Buffer controlled_buffer_13
  assign controlled_buffer_7_out[0] = controlunit_1_pc_to_bus_en ? programcounter_1_pc_out[0] : 1'bz;  // Controlled_Buffer controlled_buffer_14
  assign controlled_buffer_7_out[1] = controlunit_1_pc_to_bus_en ? programcounter_1_pc_out[1] : 1'bz;  // Controlled_Buffer controlled_buffer_15
  assign controlled_buffer_7_out[2] = controlunit_1_pc_to_bus_en ? programcounter_1_pc_out[2] : 1'bz;  // Controlled_Buffer controlled_buffer_16
  RAM ram_1 (
    .addr(MAR_q), .we(controlunit_1_ram_we), .oe(controlunit_1_ram_oe), .clk(clock_1_out),
    .dout(controlled_buffer_7_out));  // open: din
endmodule

module Adder8bit (
  input  [7:0] A,
  input  [7:0] B,
  input  Cin,
  output [7:0] SUM,
  output CarryOut
);

  wire fulladder_1_carry, fulladder_2_carry, fulladder_3_carry, fulladder_4_carry, fulladder_5_carry,
       fulladder_6_carry, fulladder_7_carry;

  FullAdder fulladder_1 (.A(A[0]), .B(B[0]), .Cin(Cin), .SUM(SUM[0]), .Carry(fulladder_1_carry));
  FullAdder fulladder_2 (.A(A[1]), .B(B[1]), .Cin(fulladder_1_carry), .SUM(SUM[1]), .Carry(fulladder_2_carry));
  FullAdder fulladder_3 (.A(A[2]), .B(B[2]), .Cin(fulladder_2_carry), .SUM(SUM[2]), .Carry(fulladder_3_carry));
  FullAdder fulladder_4 (.A(A[3]), .B(B[3]), .Cin(fulladder_3_carry), .SUM(SUM[3]), .Carry(fulladder_4_carry));
  FullAdder fulladder_5 (.A(A[4]), .B(B[4]), .Cin(fulladder_4_carry), .SUM(SUM[4]), .Carry(fulladder_5_carry));
  FullAdder fulladder_6 (.A(A[5]), .B(B[5]), .Cin(fulladder_5_carry), .SUM(SUM[5]), .Carry(fulladder_6_carry));
  FullAdder fulladder_7 (.A(A[6]), .B(B[6]), .Cin(fulladder_6_carry), .SUM(SUM[6]), .Carry(fulladder_7_carry));
  FullAdder fulladder_8 (.A(A[7]), .B(B[7]), .Cin(fulladder_7_carry), .SUM(SUM[7]), .Carry(CarryOut));
endmodule

module FullAdder (
  input  A,
  input  B,
  input  Cin,
  output SUM,
  output Carry
);

  wire and_1_out, and_2_out, xor_1_out;

  and and_1 (and_1_out, Cin, B);
  xor xor_1 (xor_1_out, Cin, B);
  xor xor_2 (SUM, Cin, B, A);
  and and_2 (and_2_out, xor_1_out, A);
  or or_1 (Carry, and_1_out, and_2_out);
endmodule

module ALU (
  input  [7:0] A,
  input  [7:0] B,
  input  [2:0] ALU_SEL,
  output CarryOut,
  output [7:0] Result,
  output Zero
);

  wire [7:0] adder8bit_1_sum, and_1_out, not_1_out, or_1_out, xor_1_out, xor_9_out;

  xor xor_1 (xor_1_out[0], B[0], ALU_SEL[0]);
  xor xor_2 (xor_1_out[1], B[1], ALU_SEL[0]);
  xor xor_3 (xor_1_out[2], B[2], ALU_SEL[0]);
  xor xor_4 (xor_1_out[3], B[3], ALU_SEL[0]);
  xor xor_5 (xor_1_out[4], B[4], ALU_SEL[0]);
  xor xor_6 (xor_1_out[5], B[5], ALU_SEL[0]);
  xor xor_7 (xor_1_out[6], B[6], ALU_SEL[0]);
  xor xor_8 (xor_1_out[7], B[7], ALU_SEL[0]);
  Adder8bit adder8bit_1 (.A(A), .B(xor_1_out), .Cin(ALU_SEL[0]), .SUM(adder8bit_1_sum), .CarryOut(CarryOut));
  not not_1 (not_1_out[0], A[0]);
  not not_2 (not_1_out[1], A[1]);
  not not_3 (not_1_out[2], A[2]);
  not not_4 (not_1_out[3], A[3]);
  not not_5 (not_1_out[4], A[4]);
  not not_6 (not_1_out[5], A[5]);
  not not_7 (not_1_out[6], A[6]);
  not not_8 (not_1_out[7], A[7]);
  xor xor_9 (xor_9_out[0], A[0], B[0]);
  xor xor_10 (xor_9_out[1], A[1], B[1]);
  xor xor_11 (xor_9_out[2], A[2], B[2]);
  xor xor_12 (xor_9_out[3], A[3], B[3]);
  xor xor_13 (xor_9_out[4], A[4], B[4]);
  xor xor_14 (xor_9_out[5], A[5], B[5]);
  xor xor_15 (xor_9_out[6], A[6], B[6]);
  xor xor_16 (xor_9_out[7], A[7], B[7]);
  and and_1 (and_1_out[0], A[0], B[0]);
  and and_2 (and_1_out[1], A[1], B[1]);
  and and_3 (and_1_out[2], A[2], B[2]);
  and and_4 (and_1_out[3], A[3], B[3]);
  and and_5 (and_1_out[4], A[4], B[4]);
  and and_6 (and_1_out[5], A[5], B[5]);
  and and_7 (and_1_out[6], A[6], B[6]);
  and and_8 (and_1_out[7], A[7], B[7]);
  or or_1 (or_1_out[0], A[0], B[0]);
  or or_2 (or_1_out[1], A[1], B[1]);
  or or_3 (or_1_out[2], A[2], B[2]);
  or or_4 (or_1_out[3], A[3], B[3]);
  or or_5 (or_1_out[4], A[4], B[4]);
  or or_6 (or_1_out[5], A[5], B[5]);
  or or_7 (or_1_out[6], A[6], B[6]);
  or or_8 (or_1_out[7], A[7], B[7]);
  Multiplexer #(.select(3), .width(8)) multiplexer_1 (
    .in0(adder8bit_1_sum), .in1(adder8bit_1_sum), .in2(and_1_out), .in3(or_1_out), .in4(xor_9_out),
    .in5(not_1_out), .in6(A), .in7({8{1'b0}}), .out(Result), .sel(ALU_SEL));
  nor nor_1 (Zero, Result[0], Result[1], Result[2], Result[3], Result[4], Result[5], Result[6], Result[7]);
endmodule

module Register8bit (
  input  WE,
  input  [7:0] D,
  input  CLK,
  output [7:0] Q
);

  wire multiplexer_1_out, multiplexer_2_out, multiplexer_3_out, multiplexer_4_out, multiplexer_5_out,
       multiplexer_6_out, multiplexer_7_out, multiplexer_8_out;

  D_Flip_Flop d_ff_1 (.D(multiplexer_1_out), .clk(CLK), .Q(Q[0]));  // open: Qn, preset, reset
  Multiplexer multiplexer_1 (.in0(Q[0]), .in1(D[0]), .out(multiplexer_1_out), .sel(WE));
  D_Flip_Flop d_ff_2 (.D(multiplexer_2_out), .clk(CLK), .Q(Q[1]));  // open: Qn, preset, reset
  Multiplexer multiplexer_2 (.in0(Q[1]), .in1(D[1]), .out(multiplexer_2_out), .sel(WE));
  D_Flip_Flop d_ff_3 (.D(multiplexer_3_out), .clk(CLK), .Q(Q[2]));  // open: Qn, preset, reset
  Multiplexer multiplexer_3 (.in0(Q[2]), .in1(D[2]), .out(multiplexer_3_out), .sel(WE));
  D_Flip_Flop d_ff_4 (.D(multiplexer_4_out), .clk(CLK), .Q(Q[3]));  // open: Qn, preset, reset
  Multiplexer multiplexer_4 (.in0(Q[3]), .in1(D[3]), .out(multiplexer_4_out), .sel(WE));
  D_Flip_Flop d_ff_5 (.D(multiplexer_5_out), .clk(CLK), .Q(Q[4]));  // open: Qn, preset, reset
  Multiplexer multiplexer_5 (.in0(Q[4]), .in1(D[4]), .out(multiplexer_5_out), .sel(WE));
  D_Flip_Flop d_ff_6 (.D(multiplexer_6_out), .clk(CLK), .Q(Q[5]));  // open: Qn, preset, reset
  Multiplexer multiplexer_6 (.in0(Q[5]), .in1(D[5]), .out(multiplexer_6_out), .sel(WE));
  D_Flip_Flop d_ff_7 (.D(multiplexer_7_out), .clk(CLK), .Q(Q[6]));  // open: Qn, preset, reset
  Multiplexer multiplexer_7 (.in0(Q[6]), .in1(D[6]), .out(multiplexer_7_out), .sel(WE));
  D_Flip_Flop d_ff_8 (.D(multiplexer_8_out), .clk(CLK), .Q(Q[7]));  // open: Qn, preset, reset
  Multiplexer multiplexer_8 (.in0(Q[7]), .in1(D[7]), .out(multiplexer_8_out), .sel(WE));
endmodule

module ProgramCounter (
  input  PC_Load,
  input  PC_WE,
  input  CLK,
  input  [7:0] Data_IN,
  output [7:0] PC_OUT
);

  wire [7:0] adder8bit_1_sum, multiplexer_1_out;

  Register8bit register8bit_1 (.WE(PC_WE), .D(multiplexer_1_out), .CLK(CLK), .Q(PC_OUT));
  Adder8bit adder8bit_1 (.A(PC_OUT), .B(8'h1), .Cin(1'b0), .SUM(adder8bit_1_sum));  // open: CarryOut
  Multiplexer #(.width(8)) multiplexer_1 (.in0(adder8bit_1_sum), .in1(Data_IN), .out(multiplexer_1_out), .sel(PC_Load));
endmodule

module ControlUnit (
  input  [3:0] OPCODE,
  input  CLK,
  input  RESET,
  output [2:0] ALU_SEL,
  output PC_Load,
  output PC_WE,
  output AC_WE,
  output IR_WE,
  output MAR_WE,
  output RAM_WE,
  output RAM_OE,
  output AC_to_Bus_EN,
  output PC_to_Bus_EN,
  output COUNTER_RESET
);

  wire or_1_out;
  wire [2:0] counter_1_q;

  or or_1 (or_1_out, RESET, COUNTER_RESET);
  Counter #(.max('h7), .width(3)) counter_1 (
    .clr(or_1_out), .load(1'b0), .up(1'b1), .clk(CLK), .Q(counter_1_q));  // open: count, D, carry
  ROM #(.addrWidth(7), .dataWidth(13)) rom_1 (
    .addr({OPCODE, counter_1_q}),
    .data({COUNTER_RESET, PC_to_Bus_EN, AC_to_Bus_EN, RAM_OE, RAM_WE, MAR_WE, IR_WE, AC_WE, PC_WE, PC_Load, ALU_SEL}));

  // Notes on the sheet:
  //   contents of rom_1 (hex, n*v repeats v):
  //   880 250 1000 5*0 880 250 880 290 1220 0 0 0 880 250 880 290 1500 0 0 0 880 250 880 290 200 1020 0 0
  //   880 250 880 290 201 1020 0 0 880 250 880 1218 4*0 880 250 1000 5*0 880 250 1000 290 4*0 880 250 1000
  //   290 4*0 880 250 1000 290 4*0 880 250 1000 290 4*0 880 250 1000 290 4*0 880 250 1000 290 4*0 880 250
  //   1000 290 4*0 880 250 1000 290 4*0 880 250 1000 290
endmodule
